// Logisim project Fetch_Decode_Completed.circ as structural Verilog
module Fetch_Unit (
  input  Reset,
  input  [15:0] PC,
  output needs_valc,
  output needs_regids,
  output mem_error,
  output [3:0] icode,
  output [3:0] ifun,
  output [3:0] rA,
  output [3:0] rB,
  output [63:0] valC,
  output [15:0] valP
);

  wire and_1_out, Clk_out, counter_1_carry, counter_2_carry, d_ff_1_q, d_ff_2_q, decoder_1_out1,
       decoder_1_out2, decoder_1_out3, decoder_1_out4, decoder_1_out5, decoder_1_out6, decoder_1_out7,
       decoder_1_out8, decoder_1_out9, decoder_1_out10, decoder_1_out11, decoder_1_out12, decoder_1_out13,
       decoder_1_out14, decoder_1_out15, decoder_2_out0, decoder_2_out1, decoder_2_out2, decoder_2_out3,
       decoder_2_out4, decoder_2_out5, decoder_2_out6, decoder_2_out7, decoder_2_out8, decoder_2_out9,
       or_1_out, or_4_out, or_5_out, or_6_out, or_7_out, or_9_out, or_10_out;
  wire [3:0] multiplexer_2_out, multiplexer_2_out_2, multiplexer_2_out_3, multiplexer_2_out_4, rom_1_data,
       rom_1_data_2;
  wire [7:0] register_1_q, register_2_q, register_3_q, register_4_q, register_5_q, register_6_q,
       register_7_q, register_8_q;
  wire [15:0] adder_1_out, adder_2_out, adder_3_out, counter_2_q, demultiplexer_1_out0, demultiplexer_1_out1,
       multiplexer_1_out;

  Counter #(.max('h7), .width(3)) counter_1 (
    .clr(Reset), .up(1'b1), .count(or_6_out), .clk(Clk_out), .carry(counter_1_carry));  // open: load, D, Q
  or or_1 (or_1_out, decoder_1_out3, decoder_1_out4, decoder_1_out5);
  or or_2 (needs_regids, or_1_out, or_5_out);
  or or_3 (needs_valc, or_1_out, or_6_out);
  or or_4 (or_4_out, decoder_1_out1, decoder_1_out9);
  D_Flip_Flop d_ff_1 (.D(or_5_out), .clk(Clk_out), .Q(d_ff_1_q));  // open: Qn, preset, reset
  or or_5 (or_5_out, decoder_1_out2, decoder_1_out6, decoder_1_out10, decoder_1_out11);
  or or_6 (or_6_out, decoder_1_out7, decoder_1_out8);
  D_Flip_Flop d_ff_2 (.D(or_7_out), .clk(Clk_out), .Q(d_ff_2_q), .reset(Reset));  // open: Qn, preset
  or or_7 (or_7_out, d_ff_2_q, counter_1_carry);
  Decoder #(.enable("false"), .select(4)) decoder_1 (
    .out1(decoder_1_out1), .out2(decoder_1_out2), .out3(decoder_1_out3), .out4(decoder_1_out4),
    .out5(decoder_1_out5), .out6(decoder_1_out6), .out7(decoder_1_out7), .out8(decoder_1_out8),
    .out9(decoder_1_out9), .out10(decoder_1_out10), .out11(decoder_1_out11), .out12(decoder_1_out12),
    .out13(decoder_1_out13), .out14(decoder_1_out14), .out15(decoder_1_out15), .sel(icode));  // open: out0
  Multiplexer #(.select(4), .width(16)) multiplexer_1 (
    .in0({16{1'b0}}), .in1(16'h1), .in2(16'h2), .in3(16'ha), .in4(16'ha), .in5(16'ha), .in6(16'h2),
    .in7(16'h9), .in8(16'h9), .in9(16'h1), .in10(16'h2), .in11(16'h2), .out(multiplexer_1_out), .sel(icode));  // open: in12, in13, in14, in15
  or or_8 (mem_error, decoder_1_out15, decoder_1_out14, decoder_1_out13, decoder_1_out12);
  Clock Clk (.out(Clk_out));
  or or_9 (or_9_out, d_ff_1_q, or_4_out, mem_error, d_ff_2_q, Reset);
  Adder #(.width(16)) adder_1 (.a(PC), .b(counter_2_q), .out(adder_1_out));  // open: cin, cout
  ROM #(.addrWidth(16)) rom_1 (.addr(adder_1_out), .data({rom_1_data_2, rom_1_data}));
  Counter #(.max('h9), .width(16)) counter_2 (
    .clr(or_9_out), .up(1'b1), .count(1'b1), .clk(Clk_out), .carry(counter_2_carry), .Q(counter_2_q));  // open: load, D
  Adder #(.width(16)) adder_2 (.a(PC), .b(multiplexer_1_out), .out(adder_2_out));  // open: cin, cout
  Demultiplexer #(.width(16)) demultiplexer_1 (
    .out0(demultiplexer_1_out0), .out1(demultiplexer_1_out1), .in(counter_2_q), .sel(or_6_out));
  or or_10 (or_10_out, counter_2_carry, or_9_out);
  Adder #(.width(16)) adder_3 (.a(demultiplexer_1_out1), .b(16'h1), .out(adder_3_out));  // open: cin, cout
  Decoder #(.enable("false"), .select(4)) decoder_2 (
    .out0(decoder_2_out0), .out1(decoder_2_out1), .out2(decoder_2_out2), .out3(decoder_2_out3),
    .out4(decoder_2_out4), .out5(decoder_2_out5), .out6(decoder_2_out6), .out7(decoder_2_out7),
    .out8(decoder_2_out8), .out9(decoder_2_out9), .sel(multiplexer_2_out));  // open: out10, out11, out12, out13, out14, out15
  Multiplexer #(.width(16)) multiplexer_2 (
    .in0(demultiplexer_1_out0), .in1(adder_3_out),
    .out({multiplexer_2_out_4, multiplexer_2_out_3, multiplexer_2_out_2, multiplexer_2_out}), .sel(and_1_out));
  and and_1 (and_1_out, or_6_out, ~d_ff_2_q);  // AND_Gate
  Register register_1 (
    .D({rom_1_data_2, rom_1_data}), .en(decoder_2_out2), .clk(Clk_out), .Q(register_1_q), .clr(Reset));
  Register register_2 (
    .D({rom_1_data_2, rom_1_data}), .en(decoder_2_out5), .clk(Clk_out), .Q(register_2_q), .clr(Reset));
  Register register_3 (
    .D({rom_1_data_2, rom_1_data}), .en(decoder_2_out6), .clk(Clk_out), .Q(register_3_q), .clr(Reset));
  Register register_4 (
    .D({rom_1_data_2, rom_1_data}), .en(decoder_2_out9), .clk(Clk_out), .Q(register_4_q), .clr(Reset));
  Register register_5 (
    .D({rom_1_data_2, rom_1_data}), .en(decoder_2_out3), .clk(Clk_out), .Q(register_5_q), .clr(Reset));
  Register register_6 (
    .D({rom_1_data_2, rom_1_data}), .en(decoder_2_out4), .clk(Clk_out), .Q(register_6_q), .clr(Reset));
  Register register_7 (
    .D({rom_1_data_2, rom_1_data}), .en(decoder_2_out7), .clk(Clk_out), .Q(register_7_q), .clr(Reset));
  Register register_8 (
    .D({rom_1_data_2, rom_1_data}), .en(decoder_2_out8), .clk(Clk_out), .Q(register_8_q), .clr(Reset));
  Register #(.width(4)) r_icode (.D(rom_1_data_2), .en(decoder_2_out0), .clk(Clk_out), .Q(icode), .clr(Reset));
  Register #(.width(4)) r_ifun (.D(rom_1_data), .en(decoder_2_out0), .clk(Clk_out), .Q(ifun), .clr(Reset));
  Register #(.width(4)) r_rA (.D(rom_1_data_2), .en(decoder_2_out1), .clk(Clk_out), .Q(rA), .clr(Reset));
  Register #(.width(4)) r_rB (.D(rom_1_data), .en(decoder_2_out1), .clk(Clk_out), .Q(rB), .clr(Reset));
  Register #(.width(64)) r_valC (
    .D({register_1_q, register_5_q, register_6_q, register_2_q, register_3_q, register_7_q, register_8_q, register_4_q}),
    .clk(Clk_out), .Q(valC), .clr(Reset));  // open: en
  Register #(.width(16)) r_valP (.D(adder_2_out), .en(or_10_out), .clk(Clk_out), .Q(valP), .clr(Reset));

  // Notes on the sheet:
  //   contents of rom_1 (hex, n*v repeats v):
  //   70 12 f2 23 4a 6d 6b 7a 9b 11 113*0 6d
endmodule

module Decode_Unit (
  input  [3:0] iCode,
  input  [3:0] rA,
  input  [3:0] rB,
  input  [3:0] valE,
  input  reset,
  input  [3:0] valM,
  output [3:0] valA,
  output [3:0] valB
);

  wire clock_1_out, counter_1_q, decoder_1_out2, decoder_1_out3, decoder_1_out5, decoder_1_out6,
       decoder_1_out8, decoder_1_out9, decoder_1_out10, decoder_1_out11, decoder_2_out8, decoder_2_out9,
       decoder_2_out10, decoder_2_out11, decoder_3_out0, decoder_3_out1, decoder_3_out2, decoder_3_out3,
       decoder_3_out4, decoder_3_out5, decoder_3_out6, decoder_3_out7, decoder_3_out8, decoder_3_out9,
       decoder_3_out10, decoder_3_out11, decoder_3_out12, decoder_3_out13, decoder_3_out14,
       multiplexer_2_out, multiplexer_4_out, not_1_out, not_2_out, or_1_out, or_2_out, or_3_out, or_4_out,
       or_5_out, or_6_out;
  wire [3:0] multiplexer_1_out, multiplexer_3_out, multiplexer_5_out, multiplexer_6_out, multiplexer_7_out,
       r8_q, r9_q, r10_q, r11_q, r12_q, r13_q, r14_q, rax_q, rbp_q, rbx_q, rcx_q, rdi_q, rdx_q, register_1_q,
       register_2_q, rsi_q, rsp_q;

  Decoder #(.select(4)) decoder_1 (
    .out2(decoder_1_out2), .out3(decoder_1_out3), .out5(decoder_1_out5), .out6(decoder_1_out6),
    .out8(decoder_1_out8), .out9(decoder_1_out9), .out10(decoder_1_out10), .out11(decoder_1_out11),
    .sel(iCode));  // open: out0, out1, out4, out7, out12, out13, out14, out15, en
  Register #(.width(4)) register_1 (.D(valE), .en(or_1_out), .clk(clock_1_out), .Q(register_1_q));  // open: clr
  Register #(.width(4)) register_2 (.D(valM), .en(decoder_1_out5), .clk(clock_1_out), .Q(register_2_q));  // open: clr
  Decoder #(.select(4)) decoder_2 (
    .out8(decoder_2_out8), .out9(decoder_2_out9), .out10(decoder_2_out10), .out11(decoder_2_out11),
    .sel(iCode));  // open: out0, out1, out2, out3, out4, out5, out6, out7, out12, out13, out14, out15, en
  or or_1 (or_1_out, decoder_1_out2, decoder_1_out3, decoder_1_out6, decoder_1_out8, decoder_1_out9, decoder_1_out10);
  or or_2 (or_2_out, decoder_2_out8, decoder_2_out9, decoder_2_out11);
  Counter #(.max('h1), .width(1)) counter_1 (
    .clr(reset), .up(1'b1), .count(decoder_1_out11), .clk(clock_1_out), .Q(counter_1_q));  // open: load, D, carry
  Multiplexer #(.width(4)) multiplexer_1 (
    .in0(register_1_q), .in1(register_2_q), .out(multiplexer_1_out), .sel(multiplexer_2_out));
  not not_1 (not_1_out, or_1_out);
  Multiplexer multiplexer_2 (.in0(not_1_out), .in1(not_2_out), .out(multiplexer_2_out), .sel(decoder_1_out11));
  or or_3 (or_3_out, decoder_1_out8, decoder_1_out9, decoder_1_out10);
  not not_2 (not_2_out, counter_1_q);
  or or_4 (or_4_out, decoder_1_out5, decoder_1_out11);
  Multiplexer #(.width(4)) multiplexer_3 (.in0(rB), .in1(rA), .out(multiplexer_3_out), .sel(or_4_out));
  Multiplexer multiplexer_4 (.in0(or_3_out), .in1(counter_1_q), .out(multiplexer_4_out), .sel(decoder_1_out11));
  Multiplexer #(.width(4)) multiplexer_5 (
    .in0(multiplexer_3_out), .in1(4'b0111), .out(multiplexer_5_out), .sel(multiplexer_4_out));
  or or_5 (or_5_out, decoder_1_out11, decoder_1_out5, or_1_out);
  Decoder #(.select(4)) decoder_3 (
    .out0(decoder_3_out0), .out1(decoder_3_out1), .out2(decoder_3_out2), .out3(decoder_3_out3),
    .out4(decoder_3_out4), .out5(decoder_3_out5), .out6(decoder_3_out6), .out7(decoder_3_out7),
    .out8(decoder_3_out8), .out9(decoder_3_out9), .out10(decoder_3_out10), .out11(decoder_3_out11),
    .out12(decoder_3_out12), .out13(decoder_3_out13), .out14(decoder_3_out14), .sel(multiplexer_5_out),
    .en(or_5_out));  // open: out15
  Clock clock_1 (.out(clock_1_out));
  or or_6 (or_6_out, decoder_2_out10, or_2_out);
  Multiplexer #(.width(4)) multiplexer_6 (.in0(rA), .in1(4'b0111), .out(multiplexer_6_out), .sel(or_2_out));
  Multiplexer #(.width(4)) multiplexer_7 (.in0(rB), .in1(4'b0111), .out(multiplexer_7_out), .sel(or_6_out));
  Register #(.width(4)) rax (.D(multiplexer_1_out), .en(decoder_3_out0), .clk(clock_1_out), .Q(rax_q), .clr(reset));
  Register #(.width(4)) rbx (.D(multiplexer_1_out), .en(decoder_3_out1), .clk(clock_1_out), .Q(rbx_q), .clr(reset));
  Register #(.width(4)) rcx (.D(multiplexer_1_out), .en(decoder_3_out2), .clk(clock_1_out), .Q(rcx_q), .clr(reset));
  Register #(.width(4)) rdx (.D(multiplexer_1_out), .en(decoder_3_out3), .clk(clock_1_out), .Q(rdx_q), .clr(reset));
  Register #(.width(4)) rsi (.D(multiplexer_1_out), .en(decoder_3_out4), .clk(clock_1_out), .Q(rsi_q), .clr(reset));
  Register #(.width(4)) rdi (.D(multiplexer_1_out), .en(decoder_3_out5), .clk(clock_1_out), .Q(rdi_q), .clr(reset));
  Register #(.width(4)) rbp (.D(multiplexer_1_out), .en(decoder_3_out6), .clk(clock_1_out), .Q(rbp_q), .clr(reset));
  Register #(.width(4)) rsp (.D(multiplexer_1_out), .en(decoder_3_out7), .clk(clock_1_out), .Q(rsp_q), .clr(reset));
  Register #(.width(4)) r8 (.D(multiplexer_1_out), .en(decoder_3_out8), .clk(clock_1_out), .Q(r8_q), .clr(reset));
  Register #(.width(4)) r9 (.D(multiplexer_1_out), .en(decoder_3_out9), .clk(clock_1_out), .Q(r9_q), .clr(reset));
  Register #(.width(4)) r10 (.D(multiplexer_1_out), .en(decoder_3_out10), .clk(clock_1_out), .Q(r10_q), .clr(reset));
  Register #(.width(4)) r11 (.D(multiplexer_1_out), .en(decoder_3_out11), .clk(clock_1_out), .Q(r11_q), .clr(reset));
  Register #(.width(4)) r12 (.D(multiplexer_1_out), .en(decoder_3_out12), .clk(clock_1_out), .Q(r12_q), .clr(reset));
  Register #(.width(4)) r13 (.D(multiplexer_1_out), .en(decoder_3_out13), .clk(clock_1_out), .Q(r13_q), .clr(reset));
  Register #(.width(4)) r14 (.D(multiplexer_1_out), .en(decoder_3_out14), .clk(clock_1_out), .Q(r14_q), .clr(reset));
  Multiplexer #(.select(4), .width(4)) multiplexer_8 (
    .in0(rax_q), .in1(rbx_q), .in2(rcx_q), .in3(rdx_q), .in4(rsi_q), .in5(rdi_q), .in6(rbp_q), .in7(rsp_q),
    .in8(r8_q), .in9(r9_q), .in10(r10_q), .in11(r11_q), .in12(r12_q), .in13(r13_q), .in14(r14_q), .out(valA),
    .sel(multiplexer_6_out));  // open: in15
  Multiplexer #(.select(4), .width(4)) multiplexer_9 (
    .in0(rax_q), .in1(rbx_q), .in2(rcx_q), .in3(rdx_q), .in4(rsi_q), .in5(rdi_q), .in6(rbp_q), .in7(rsp_q),
    .in8(r8_q), .in9(r9_q), .in10(r10_q), .in11(r11_q), .in12(r12_q), .in13(r13_q), .in14(r14_q), .out(valB),
    .sel(multiplexer_7_out));  // open: in15
endmodule
