// Logisim project Fetch_NoFlagsOrWorkingInstructions.circ as structural Verilog
module Fetch_Unit (
  input  in_1,
  input  in_2,
  input  in_3,
  input  in_4,
  input  [7:0] in_5,
  output mem_error
);

  wire and_1_out, and_2_out, and_3_out, clock_1_out, clock_2_out, counter_1_carry, decoder_1_out0,
       decoder_1_out1, decoder_1_out2, decoder_1_out3, decoder_1_out4, decoder_1_out5, decoder_1_out6,
       decoder_1_out7, decoder_1_out8, decoder_1_out9, or_1_out, or_2_out;
  wire [3:0] counter_1_q, counter_1_q_2, register_1_q, register_2_q;
  wire [7:0] adder_1_out, rom_1_data;

  ROM rom_1 (.addr(adder_1_out), .data(rom_1_data));
  not not_1 (mem_error, or_1_out);
  Counter #(.max('h9)) counter_1 (
    .clr(in_2), .up(in_3), .count(in_4), .clk(clock_1_out), .carry(counter_1_carry),
    .Q({counter_1_q_2, counter_1_q}));  // open: load, D
  Clock clock_1 (.out(clock_1_out));
  Adder adder_1 (.a({counter_1_q_2, counter_1_q}), .b(in_5), .out(adder_1_out));  // open: cin, cout
  or or_1 (or_1_out, and_3_out, or_2_out);
  or or_2 (or_2_out, and_1_out, and_2_out);
  Clock clock_2 (.out(clock_2_out));
  and and_1 (and_1_out, register_1_q[1], ~register_1_q[0], ~register_1_q[3]);  // AND_Gate
  and and_2 (and_2_out, register_1_q[1], register_1_q[2]);
  Decoder #(.select(4)) decoder_1 (
    .out0(decoder_1_out0), .out1(decoder_1_out1), .out2(decoder_1_out2), .out3(decoder_1_out3),
    .out4(decoder_1_out4), .out5(decoder_1_out5), .out6(decoder_1_out6), .out7(decoder_1_out7),
    .out8(decoder_1_out8), .out9(decoder_1_out9), .sel(counter_1_q), .en(in_1));  // open: out10, out11, out12, out13, out14, out15
  Register #(.width(4)) register_1 (
    .D(rom_1_data[7:4]), .en(decoder_1_out0), .clk(clock_2_out), .Q(register_1_q));  // open: clr
  Register #(.width(4)) register_2 (
    .D(rom_1_data[3:0]), .en(decoder_1_out0), .clk(clock_2_out), .Q(register_2_q));  // open: clr
  Register #(.width(4)) register_3 (.D(rom_1_data[7:4]), .en(decoder_1_out1), .clk(clock_2_out));  // open: Q, clr
  Register #(.width(4)) register_4 (.D(rom_1_data[3:0]), .en(decoder_1_out1), .clk(clock_2_out));  // open: Q, clr
  Register register_5 (.D(rom_1_data), .en(decoder_1_out2), .clk(clock_2_out));  // open: Q, clr
  Register register_6 (.D(rom_1_data), .en(decoder_1_out3), .clk(clock_2_out));  // open: Q, clr
  Register register_7 (.D(rom_1_data), .en(decoder_1_out4), .clk(clock_2_out));  // open: Q, clr
  Register register_8 (.D(rom_1_data), .en(decoder_1_out5), .clk(clock_2_out));  // open: Q, clr
  Register register_9 (.D(rom_1_data), .en(decoder_1_out6), .clk(clock_2_out));  // open: Q, clr
  Register register_10 (.D(rom_1_data), .en(decoder_1_out7), .clk(clock_2_out));  // open: Q, clr
  Register register_11 (.D(rom_1_data), .en(decoder_1_out8), .clk(clock_2_out));  // open: Q, clr
  Register register_12 (.D(rom_1_data), .en(decoder_1_out9), .clk(clock_2_out));  // open: Q, clr
  Register register_13 (.D(adder_1_out), .en(counter_1_carry), .clk(clock_1_out));  // open: Q, clr
  and and_3 (and_3_out, ~register_2_q[3], ~register_2_q[2], ~register_2_q[1], ~register_2_q[0]);  // AND_Gate

  // Notes on the sheet:
  //   contents of rom_1 (hex, n*v repeats v):
  //   49 6e 20 61 20 70 79 74 68 6f 6e 20 65 6e 76 69 72 6f 6e 6d 65 6e 74 2c 20 72 75 6e 20 74 68 65 20
  //   66 6f 6c 6c 6f 77 69 6e 67 20 63 6f 6d 6d 61 6e 64 a a 70 79 74 68 6f 6e 20 79 6f 32 6d 65 6d 2e 70
  //   79 20 2d 2d 79 6f 20 3c 73 6f 75 72 63 65 5f 66 69 6c 65 5f 6e 61 6d 65 3e 2e 79 6f 20 2d 2d 6d 65
  //   6d 20 3c 6d 65 6d 6f 72 79 5f 66 69 6c 65 5f 6e 61 6d 65 3e 2e 6d 65 6d
endmodule
