// Logisim project Fetch_complete.circ as structural Verilog: 2 circuits, main circuit main
module main (
);

  wire demultiplexer_1_out2, demultiplexer_1_out4, demultiplexer_1_out5, demultiplexer_1_out6,
       demultiplexer_1_out8, demultiplexer_1_out9, demultiplexer_1_out10, demultiplexer_1_out11, or_1_out,
       or_2_out;
  wire [3:0] fetch_unit_1_icode_out;

  Fetch_Unit fetch_unit_1 (.icode_out(fetch_unit_1_icode_out));  // open: Reset, PC, mem_error, ifun_out, rA_out, rB_out, valC_out, valP_out
  Demultiplexer #(.select(4)) demultiplexer_1 (
    .out2(demultiplexer_1_out2), .out4(demultiplexer_1_out4), .out5(demultiplexer_1_out5),
    .out6(demultiplexer_1_out6), .out8(demultiplexer_1_out8), .out9(demultiplexer_1_out9),
    .out10(demultiplexer_1_out10), .out11(demultiplexer_1_out11), .in(1'b1), .sel(fetch_unit_1_icode_out));  // open: out0, out1, out3, out7, out12, out13, out14, out15
  or or_1 (or_1_out, demultiplexer_1_out2, demultiplexer_1_out4, demultiplexer_1_out5, demultiplexer_1_out6);
  or or_2 (or_2_out, demultiplexer_1_out8, demultiplexer_1_out9, demultiplexer_1_out11);

  // Notes on the sheet:
  //   load_rarb
  //   load_rsp
  //   load_rspra
endmodule

module Fetch_Unit (
  input  Reset,
  input  [15:0] PC,
  output mem_error,
  output [3:0] icode_out,
  output [3:0] ifun_out,
  output [3:0] rA_out,
  output [3:0] rB_out,
  output [63:0] valC_out,
  output [15:0] valP_out
);

  wire and_1_out, Clk_out, counter_1_carry, counter_2_carry, d_ff_1_q, d_ff_2_q, decoder_1_out1,
       decoder_1_out2, decoder_1_out3, decoder_1_out4, decoder_1_out5, decoder_1_out6, decoder_1_out7,
       decoder_1_out8, decoder_1_out9, decoder_1_out10, decoder_1_out11, decoder_1_out12, decoder_1_out13,
       decoder_1_out14, decoder_1_out15, decoder_2_out0, decoder_2_out1, decoder_2_out2, decoder_2_out3,
       decoder_2_out4, decoder_2_out5, decoder_2_out6, decoder_2_out7, decoder_2_out8, decoder_2_out9,
       or_1_out, or_2_out, or_3_out, or_4_out, or_5_out, or_6_out, or_7_out, or_9_out, or_10_out;
  wire [3:0] multiplexer_2_out, multiplexer_2_out_2, multiplexer_2_out_3, multiplexer_2_out_4, rom_1_data,
       rom_1_data_2;
  wire [7:0] register_1_q, register_2_q, register_3_q, register_4_q, register_5_q, register_6_q,
       register_7_q, register_8_q;
  wire [15:0] adder_1_out, adder_2_out, adder_3_out, counter_2_q, demultiplexer_1_out0, demultiplexer_1_out1,
       multiplexer_1_out;

  or or_1 (or_1_out, or_3_out, or_5_out);
  or or_2 (or_2_out, or_3_out, or_6_out);
  Counter #(.max('h7), .width(3)) counter_1 (
    .clr(Reset), .up(1'b1), .count(or_6_out), .clk(Clk_out), .carry(counter_1_carry));  // open: load, D, Q
  or or_3 (or_3_out, decoder_1_out3, decoder_1_out4, decoder_1_out5);
  or or_4 (or_4_out, decoder_1_out1, decoder_1_out9);
  or or_5 (or_5_out, decoder_1_out2, decoder_1_out6, decoder_1_out10, decoder_1_out11);
  D_Flip_Flop d_ff_1 (.D(or_5_out), .clk(Clk_out), .Q(d_ff_1_q));  // open: Qn, preset, reset
  or or_6 (or_6_out, decoder_1_out7, decoder_1_out8);
  D_Flip_Flop d_ff_2 (.D(or_7_out), .clk(Clk_out), .Q(d_ff_2_q), .reset(Reset));  // open: Qn, preset
  or or_7 (or_7_out, d_ff_2_q, counter_1_carry);
  Decoder #(.enable("false"), .select(4)) decoder_1 (
    .out1(decoder_1_out1), .out2(decoder_1_out2), .out3(decoder_1_out3), .out4(decoder_1_out4),
    .out5(decoder_1_out5), .out6(decoder_1_out6), .out7(decoder_1_out7), .out8(decoder_1_out8),
    .out9(decoder_1_out9), .out10(decoder_1_out10), .out11(decoder_1_out11), .out12(decoder_1_out12),
    .out13(decoder_1_out13), .out14(decoder_1_out14), .out15(decoder_1_out15), .sel(icode_out));  // open: out0
  Multiplexer #(.select(4), .width(16)) multiplexer_1 (
    .in0({16{1'b0}}), .in1(16'h1), .in2(16'h2), .in3(16'ha), .in4(16'ha), .in5(16'ha), .in6(16'h2),
    .in7(16'h9), .in8(16'h9), .in9(16'h1), .in10(16'h2), .in11(16'h2), .out(multiplexer_1_out),
    .sel(icode_out));  // open: in12, in13, in14, in15
  or or_8 (mem_error, decoder_1_out15, decoder_1_out14, decoder_1_out13, decoder_1_out12);
  Clock Clk (.out(Clk_out));
  ROM #(.addrWidth(16)) rom_1 (.addr(adder_1_out), .data({rom_1_data_2, rom_1_data}));
  or or_9 (or_9_out, d_ff_1_q, or_4_out, mem_error, d_ff_2_q, Reset);
  Adder #(.width(16)) adder_1 (.a(PC), .b(counter_2_q), .out(adder_1_out));  // open: cin, cout
  Counter #(.max('h9), .width(16)) counter_2 (
    .clr(or_9_out), .up(1'b1), .count(1'b1), .clk(Clk_out), .carry(counter_2_carry), .Q(counter_2_q));  // open: load, D
  Adder #(.width(16)) adder_2 (.a(PC), .b(multiplexer_1_out), .out(adder_2_out));  // open: cin, cout
  Demultiplexer #(.width(16)) demultiplexer_1 (
    .out0(demultiplexer_1_out0), .out1(demultiplexer_1_out1), .in(counter_2_q), .sel(or_6_out));
  or or_10 (or_10_out, counter_2_carry, or_9_out);
  Adder #(.width(16)) adder_3 (.a(demultiplexer_1_out1), .b(16'h1), .out(adder_3_out));  // open: cin, cout
  and and_1 (and_1_out, or_6_out, ~d_ff_2_q);  // AND_Gate
  Decoder #(.enable("false"), .select(4)) decoder_2 (
    .out0(decoder_2_out0), .out1(decoder_2_out1), .out2(decoder_2_out2), .out3(decoder_2_out3),
    .out4(decoder_2_out4), .out5(decoder_2_out5), .out6(decoder_2_out6), .out7(decoder_2_out7),
    .out8(decoder_2_out8), .out9(decoder_2_out9), .sel(multiplexer_2_out));  // open: out10, out11, out12, out13, out14, out15
  Multiplexer #(.width(16)) multiplexer_2 (
    .in0(demultiplexer_1_out0), .in1(adder_3_out),
    .out({multiplexer_2_out_4, multiplexer_2_out_3, multiplexer_2_out_2, multiplexer_2_out}), .sel(and_1_out));
  Register register_1 (
    .D({rom_1_data_2, rom_1_data}), .en(decoder_2_out2), .clk(Clk_out), .Q(register_1_q), .clr(Reset));
  Register register_2 (
    .D({rom_1_data_2, rom_1_data}), .en(decoder_2_out5), .clk(Clk_out), .Q(register_2_q), .clr(Reset));
  Register register_3 (
    .D({rom_1_data_2, rom_1_data}), .en(decoder_2_out3), .clk(Clk_out), .Q(register_3_q), .clr(Reset));
  Register register_4 (
    .D({rom_1_data_2, rom_1_data}), .en(decoder_2_out6), .clk(Clk_out), .Q(register_4_q), .clr(Reset));
  Register register_5 (
    .D({rom_1_data_2, rom_1_data}), .en(decoder_2_out9), .clk(Clk_out), .Q(register_5_q), .clr(Reset));
  Register register_6 (
    .D({rom_1_data_2, rom_1_data}), .en(decoder_2_out7), .clk(Clk_out), .Q(register_6_q), .clr(Reset));
  Register register_7 (
    .D({rom_1_data_2, rom_1_data}), .en(decoder_2_out4), .clk(Clk_out), .Q(register_7_q), .clr(Reset));
  Register register_8 (
    .D({rom_1_data_2, rom_1_data}), .en(decoder_2_out8), .clk(Clk_out), .Q(register_8_q), .clr(Reset));
  Register #(.width(4)) icode (.D(rom_1_data_2), .en(decoder_2_out0), .clk(Clk_out), .Q(icode_out), .clr(Reset));
  Register #(.width(4)) ifun (.D(rom_1_data), .en(decoder_2_out0), .clk(Clk_out), .Q(ifun_out), .clr(Reset));
  Register #(.width(4)) rA (.D(rom_1_data_2), .en(decoder_2_out1), .clk(Clk_out), .Q(rA_out), .clr(Reset));
  Register #(.width(4)) rB (.D(rom_1_data), .en(decoder_2_out1), .clk(Clk_out), .Q(rB_out), .clr(Reset));
  Register #(.width(64)) valC (
    .D({register_1_q, register_3_q, register_7_q, register_2_q, register_4_q, register_6_q, register_8_q, register_5_q}),
    .clk(Clk_out), .Q(valC_out), .clr(Reset));  // open: en
  Register #(.width(16)) valP (.D(adder_2_out), .en(or_10_out), .clk(Clk_out), .Q(valP_out), .clr(Reset));

  // Notes on the sheet:
  //   needs_regids
  //   needs_valc
  //   contents of rom_1 (hex, n*v repeats v):
  //   70 12 f2 23 4a 6d 6b 7a 9b 11 113*0 6d
endmodule
