// Logisim project FullCPU_AutoTime.circ as structural Verilog: 6 circuits, main circuit main
module main (
  input  reset,
  output fetchEnable,
  output decodeEnable,
  output executeEnable,
  output memoryEnable,
  output write_backEnable,
  output [63:0] r10,
  output PCUpdate_Enable,
  output [63:0] rdi,
  output [63:0] rax,
  output [63:0] r11,
  output [63:0] rbp,
  output [63:0] rbx,
  output [63:0] r12,
  output [63:0] rsp,
  output [63:0] rcx,
  output [63:0] r13,
  output [63:0] r8,
  output [63:0] rdx,
  output [63:0] r14,
  output [63:0] r9,
  output [63:0] rsi
);

  wire and_1_out, and_2_out, clock_1_out, comparator_1_gt, comparator_2_eq, comparator_2_lt, comparator_3_lt,
       controlled_buffer_20_out, execute_unit_1_cond, execute_unit_1_overf, execute_unit_1_sf,
       execute_unit_1_zf, fetch_unit_1_halt, fetch_unit_1_mem_error, memory_unit_1_r_enable,
       memory_unit_1_w_enable, nor_1_out, or_1_out, or_2_out, register_4_q;
  wire [2:0] multiplexer_2_out;
  wire [3:0] controlled_buffer_2_out, controlled_buffer_3_out, controlled_buffer_4_out,
       controlled_buffer_7_out, controlled_buffer_11_out, controlled_buffer_12_out, controlled_buffer_16_out,
       fetch_unit_1_icode, fetch_unit_1_ifun, fetch_unit_1_ra, fetch_unit_1_rb, icode_q, ifun_q, rA_q, rB_q;
  wire [4:0] multiplexer_2_out_2;
  wire [7:0] adder_1_out, adder_2_out, multiplexer_1_out, register_2_q, register_3_q, rom_1_data;
  wire [15:0] addr_q, fetch_unit_1_pc_addr, memory_unit_1_addr;
  wire [63:0] controlled_buffer_1_out, controlled_buffer_5_out, controlled_buffer_6_out,
       controlled_buffer_8_out, controlled_buffer_9_out, controlled_buffer_10_out, controlled_buffer_13_out,
       controlled_buffer_14_out, controlled_buffer_15_out, controlled_buffer_17_out,
       controlled_buffer_18_out, controlled_buffer_19_out, data_q, decode_unit_1_vala, decode_unit_1_valb,
       execute_unit_1_vale, fetch_unit_1_valc, fetch_unit_1_valp, memory_unit_1_data, pcupdate_unit_1_pc,
       ram_1_dout, register_1_q, valA_q, valB_q, valC_q, valE_q, valM_q, valP_q;

  Clock clock_1 (.out(clock_1_out));
  and and_1 (and_1_out, clock_1_out, ~or_1_out);  // AND_Gate
  Register #(.width(64)) register_1 (
    .D(pcupdate_unit_1_pc), .en(PCUpdate_Enable), .clk(and_1_out), .Q(register_1_q), .clr(reset));
  Comparator #(.width(64)) comparator_1 (.a(register_1_q), .b(64'hffff), .gt(comparator_1_gt));  // open: eq, lt
  Register register_2 (.D(multiplexer_1_out), .clk(and_1_out), .Q(register_2_q), .clr(reset));  // open: en
  assign controlled_buffer_1_out = fetchEnable ? register_1_q : 64'bz;  // Controlled_Buffer controlled_buffer_1
  Decoder #(.select(3)) decoder_1 (
    .out2(fetchEnable), .out3(decodeEnable), .out4(executeEnable), .out5(memoryEnable),
    .out6(write_backEnable), .out7(PCUpdate_Enable), .sel(multiplexer_2_out));  // open: out0, out1, en
  Adder adder_1 (.a(8'h1), .b(register_2_q), .out(adder_1_out));  // open: cin, cout
  ROM #(.addrWidth(16)) rom_1 (.addr(fetch_unit_1_pc_addr), .data(rom_1_data));
  Multiplexer #(.width(8)) multiplexer_1 (
    .in0({8{1'b0}}), .in1(adder_1_out), .out(multiplexer_1_out), .sel(comparator_2_lt));
  Comparator comparator_2 (.a(adder_1_out), .b(8'h16), .eq(comparator_2_eq), .lt(comparator_2_lt));  // open: gt
  Register register_3 (
    .D({multiplexer_2_out_2, multiplexer_2_out}), .clk(comparator_2_eq), .Q(register_3_q), .clr(reset));  // open: en
  LED AOK (.in(nor_1_out));
  LED INS (.in(fetch_unit_1_mem_error));
  LED HLT (.in(fetch_unit_1_halt));
  LED ADR (.in(comparator_1_gt));
  Multiplexer #(.width(8)) multiplexer_2 (
    .in0({8{1'b0}}), .in1(adder_2_out), .out({multiplexer_2_out_2, multiplexer_2_out}), .sel(comparator_3_lt));
  Adder adder_2 (.a(8'h1), .b(register_3_q), .out(adder_2_out));  // open: cin, cout
  Comparator comparator_3 (.a(adder_2_out), .b(8'h8), .lt(comparator_3_lt));  // open: gt, eq
  Fetch_Unit fetch_unit_1 (
    .Reset(reset), .Inst_Comp(rom_1_data), .PC(controlled_buffer_1_out), .mem_error(fetch_unit_1_mem_error),
    .icode(fetch_unit_1_icode), .ifun(fetch_unit_1_ifun), .PC_Addr(fetch_unit_1_pc_addr),
    .rA(fetch_unit_1_ra), .rB(fetch_unit_1_rb), .valC(fetch_unit_1_valc), .valP(fetch_unit_1_valp),
    .halt(fetch_unit_1_halt));  // open: in_4, needs_valc, needs_regids
  or or_1 (or_1_out, comparator_1_gt, fetch_unit_1_halt, fetch_unit_1_mem_error);
  Register #(.width(4)) icode (.D(fetch_unit_1_icode), .en(fetchEnable), .clk(and_1_out), .Q(icode_q), .clr(reset));
  Register #(.width(4)) ifun (.D(fetch_unit_1_ifun), .en(fetchEnable), .clk(and_1_out), .Q(ifun_q), .clr(reset));
  Register #(.width(4)) rA (.D(fetch_unit_1_ra), .en(fetchEnable), .clk(and_1_out), .Q(rA_q), .clr(reset));
  Register #(.width(4)) rB (.D(fetch_unit_1_rb), .en(fetchEnable), .clk(and_1_out), .Q(rB_q), .clr(reset));
  Register #(.width(64)) valC (.D(fetch_unit_1_valc), .en(fetchEnable), .clk(and_1_out), .Q(valC_q), .clr(reset));
  Register #(.width(64)) valP (.D(fetch_unit_1_valp), .en(fetchEnable), .clk(and_1_out), .Q(valP_q), .clr(reset));
  nor nor_1 (nor_1_out, comparator_1_gt, fetch_unit_1_halt, fetch_unit_1_mem_error);
  or or_2 (or_2_out, decodeEnable, write_backEnable);
  assign controlled_buffer_2_out = or_2_out ? icode_q : 4'bz;  // Controlled_Buffer controlled_buffer_2
  assign controlled_buffer_3_out = or_2_out ? rA_q : 4'bz;  // Controlled_Buffer controlled_buffer_3
  assign controlled_buffer_4_out = or_2_out ? rB_q : 4'bz;  // Controlled_Buffer controlled_buffer_4
  assign controlled_buffer_5_out = write_backEnable ? valE_q : 64'bz;  // Controlled_Buffer controlled_buffer_5
  assign controlled_buffer_6_out = write_backEnable ? valM_q : 64'bz;  // Controlled_Buffer controlled_buffer_6
  assign controlled_buffer_7_out = memoryEnable ? icode_q : 4'bz;  // Controlled_Buffer controlled_buffer_7
  assign controlled_buffer_8_out = memoryEnable ? valE_q : 64'bz;  // Controlled_Buffer controlled_buffer_8
  assign controlled_buffer_9_out = memoryEnable ? valA_q : 64'bz;  // Controlled_Buffer controlled_buffer_9
  assign controlled_buffer_10_out = memoryEnable ? valP_q : 64'bz;  // Controlled_Buffer controlled_buffer_10
  Memory_Unit memory_unit_1 (
    .iCode(controlled_buffer_7_out), .valE(controlled_buffer_8_out), .valA(controlled_buffer_9_out),
    .valP(controlled_buffer_10_out), .w_Enable(memory_unit_1_w_enable), .r_Enable(memory_unit_1_r_enable),
    .Addr(memory_unit_1_addr), .Data(memory_unit_1_data));
  Decode_Unit decode_unit_1 (
    .iCode(controlled_buffer_2_out), .rA(controlled_buffer_3_out), .rB(controlled_buffer_4_out),
    .write_enable(write_backEnable), .valE(controlled_buffer_5_out), .reset(reset),
    .valM(controlled_buffer_6_out), .cond(register_4_q), .valA(decode_unit_1_vala),
    .valB(decode_unit_1_valb), .reg14(r14), .reg9(r9), .regsi(rsi), .reg13(r13), .reg8(r8), .regdx(rdx),
    .reg12(r12), .regsp(rsp), .regcx(rcx), .reg11(r11), .regbp(rbp), .regbx(rbx), .reg10(r10), .regdi(rdi),
    .regax(rax));
  Register #(.width(64)) valA (.D(decode_unit_1_vala), .en(decodeEnable), .clk(and_1_out), .Q(valA_q), .clr(reset));
  Register #(.width(64)) valB (.D(decode_unit_1_valb), .en(decodeEnable), .clk(and_1_out), .Q(valB_q), .clr(reset));
  Register #(.width(16)) addr (.D(memory_unit_1_addr), .en(memoryEnable), .clk(and_1_out), .Q(addr_q), .clr(reset));
  Register #(.width(64)) data (.D(memory_unit_1_data), .en(memoryEnable), .clk(and_1_out), .Q(data_q), .clr(reset));
  RAM #(.addrWidth(16), .dataWidth(64)) ram_1 (
    .addr(addr_q), .we(memory_unit_1_w_enable), .oe(memory_unit_1_r_enable), .clk(and_1_out), .din(data_q),
    .dout(ram_1_dout));
  assign controlled_buffer_11_out = executeEnable ? icode_q : 4'bz;  // Controlled_Buffer controlled_buffer_11
  assign controlled_buffer_12_out = executeEnable ? ifun_q : 4'bz;  // Controlled_Buffer controlled_buffer_12
  assign controlled_buffer_13_out = executeEnable ? valA_q : 64'bz;  // Controlled_Buffer controlled_buffer_13
  assign controlled_buffer_14_out = executeEnable ? valC_q : 64'bz;  // Controlled_Buffer controlled_buffer_14
  assign controlled_buffer_15_out = executeEnable ? valB_q : 64'bz;  // Controlled_Buffer controlled_buffer_15
  Register #(.width(64)) valM (.D(ram_1_dout), .en(and_2_out), .clk(and_1_out), .Q(valM_q), .clr(reset));
  and and_2 (and_2_out, memoryEnable, memory_unit_1_r_enable);
  Execute_Unit execute_unit_1 (
    .iCode(controlled_buffer_11_out), .iFun(controlled_buffer_12_out), .valA(controlled_buffer_13_out),
    .valC(controlled_buffer_14_out), .valB(controlled_buffer_15_out), .COND(execute_unit_1_cond),
    .ZF(execute_unit_1_zf), .SF(execute_unit_1_sf), .OverF(execute_unit_1_overf), .valE(execute_unit_1_vale));
  Register #(.width(1)) register_4 (
    .D(execute_unit_1_cond), .en(executeEnable), .clk(and_1_out), .Q(register_4_q), .clr(reset));
  Register #(.width(1)) register_5 (
    .D(execute_unit_1_zf), .en(executeEnable), .clk(and_1_out), .clr(reset));  // open: Q
  Register #(.width(1)) register_6 (
    .D(execute_unit_1_sf), .en(executeEnable), .clk(and_1_out), .clr(reset));  // open: Q
  Register #(.width(1)) register_7 (
    .D(execute_unit_1_overf), .en(executeEnable), .clk(and_1_out), .clr(reset));  // open: Q
  Register #(.width(64)) valE (.D(execute_unit_1_vale), .en(executeEnable), .clk(and_1_out), .Q(valE_q), .clr(reset));
  assign controlled_buffer_16_out = PCUpdate_Enable ? icode_q : 4'bz;  // Controlled_Buffer controlled_buffer_16
  assign controlled_buffer_17_out = PCUpdate_Enable ? valP_q : 64'bz;  // Controlled_Buffer controlled_buffer_17
  assign controlled_buffer_18_out = PCUpdate_Enable ? valC_q : 64'bz;  // Controlled_Buffer controlled_buffer_18
  assign controlled_buffer_19_out = PCUpdate_Enable ? valM_q : 64'bz;  // Controlled_Buffer controlled_buffer_19
  assign controlled_buffer_20_out = PCUpdate_Enable ? register_4_q : 1'bz;  // Controlled_Buffer controlled_buffer_20
  PCUpdate_Unit pcupdate_unit_1 (
    .iCode(controlled_buffer_16_out), .valP(controlled_buffer_17_out), .valC(controlled_buffer_18_out),
    .valM(controlled_buffer_19_out), .CND(controlled_buffer_20_out), .PC(pcupdate_unit_1_pc));

  // Notes on the sheet:
  //   contents of rom_1 (hex, n*v repeats v):
  //   30 f0 0 1 6*0 30 f3 0 2 6*0 30 f6 0 3 6*0 30 fa 1 7*0 40 a0 8*0 30 fb 2 7*0 40 b0 8 7*0 30 fc 3 7*0
  //   40 c0 10 7*0 30 fa 2 7*0 40 a0 18 7*0 30 fb 1 7*0 40 b0 20 7*0 30 fc 3 7*0 40 c0 28 7*0 30 fa 3 7*0
  //   40 a0 30 7*0 30 fb 2 7*0 40 b0 38 7*0 30 fc 1 7*0 40 c0 40 7*0 30 fa 1 7*0 40 a3 8*0 30 fb 2 7*0 40
  //   b3 8 7*0 30 fc 1 7*0 40 c3 10 7*0 30 fa 3 7*0 40 a3 18 7*0 30 fb 1 7*0 40 b3 20 7*0 30 fc 1 7*0 40
  //   c3 28 7*0 30 fa 1 7*0 40 a3 30 7*0 30 fb 1 7*0 40 b3 38 7*0 30 fc 1 7*0 40 c3 40 7*0 30 f7 8*0 30 f8
  //   8*0 30 f9 8*0 30 fe 8*0 50 a0 8*0 50 b3 8*0 30 fc 8*0 30 f1 8*0 20 b2 62 22 71 5 2 6*0 60 ac 30 f1 1
  //   7*0 60 11 61 1b 76 e3 1 6*0 70 1e 2 6*0 61 ac 30 f1 1 7*0 60 11 60 1b 72 5 2 6*0 60 c9 30 fa 1 7*0
  //   60 ae 30 fb 3 7*0 61 eb 74 ae 1 6*0 40 96 8*0 30 fa 1 7*0 60 a8 30 fb 3 7*0 61 8b 74 9a 1 6*0 30 fa
  //   1 7*0 60 a7 30 fb 3 7*0 61 7b 74 90 1
endmodule

module Fetch_Unit (
  input  Reset,
  input  [7:0] Inst_Comp,
  input  [63:0] PC,
  input  [47:0] in_4,
  output needs_valc,
  output needs_regids,
  output mem_error,
  output [3:0] icode,
  output [3:0] ifun,
  output [15:0] PC_Addr,
  output [3:0] rA,
  output [3:0] rB,
  output [63:0] valC,
  output [63:0] valP,
  output halt
);

  wire and_1_out, and_2_out, and_3_out, and_4_out, Clk_out, counter_1_carry, decoder_1_out0, decoder_1_out1,
       decoder_1_out2, decoder_1_out3, decoder_1_out4, decoder_1_out5, decoder_1_out6, decoder_1_out7,
       decoder_1_out8, decoder_1_out9, decoder_1_out10, decoder_1_out11, decoder_1_out12, decoder_1_out13,
       decoder_1_out14, decoder_1_out15, decoder_2_out0, decoder_2_out2, decoder_3_out1, decoder_3_out2,
       decoder_3_out3, decoder_3_out4, decoder_3_out5, decoder_3_out6, decoder_3_out7, decoder_3_out8,
       decoder_4_out0, decoder_4_out1, decoder_4_out2, decoder_4_out3, decoder_4_out4, decoder_4_out5,
       decoder_4_out6, decoder_4_out7, decoder_4_out8, decoder_4_out9, or_1_out, or_4_out, or_5_out,
       or_6_out, or_8_out, or_9_out, or_10_out, or_11_out, or_12_out, or_13_out, or_14_out, or_15_out,
       or_16_out, or_17_out, or_18_out, register_9_q;
  wire [3:0] counter_1_q, counter_1_q_2, counter_1_q_3, counter_1_q_4, demultiplexer_1_out0,
       demultiplexer_1_out1;
  wire [7:0] register_1_q, register_2_q, register_3_q, register_4_q, register_5_q, register_6_q,
       register_7_q, register_8_q;
  wire [15:0] adder_2_out, multiplexer_1_out;

  or or_1 (or_1_out, decoder_1_out3, decoder_1_out4, decoder_1_out5);
  or or_2 (needs_regids, or_1_out, or_5_out);
  or or_3 (needs_valc, or_1_out, or_6_out);
  or or_4 (or_4_out, decoder_1_out1, decoder_1_out9);
  or or_5 (or_5_out, decoder_1_out2, decoder_1_out6, decoder_1_out10, decoder_1_out11);
  Decoder #(.enable("false"), .select(4)) decoder_1 (
    .out0(decoder_1_out0), .out1(decoder_1_out1), .out2(decoder_1_out2), .out3(decoder_1_out3),
    .out4(decoder_1_out4), .out5(decoder_1_out5), .out6(decoder_1_out6), .out7(decoder_1_out7),
    .out8(decoder_1_out8), .out9(decoder_1_out9), .out10(decoder_1_out10), .out11(decoder_1_out11),
    .out12(decoder_1_out12), .out13(decoder_1_out13), .out14(decoder_1_out14), .out15(decoder_1_out15),
    .sel(icode));
  or or_6 (or_6_out, decoder_1_out7, decoder_1_out8);
  Multiplexer #(.select(4), .width(16)) multiplexer_1 (
    .in0({16{1'b0}}), .in1(16'h1), .in2(16'h2), .in3(16'ha), .in4(16'ha), .in5(16'ha), .in6(16'h2),
    .in7(16'h9), .in8(16'h9), .in9(16'h1), .in10(16'h2), .in11(16'h2), .out(multiplexer_1_out), .sel(icode));  // open: in12, in13, in14, in15
  or or_7 (mem_error, decoder_1_out15, decoder_1_out14, decoder_1_out13, decoder_1_out12);
  Clock Clk (.out(Clk_out));
  or or_8 (or_8_out, and_2_out, or_4_out, mem_error, Reset);
  or or_9 (or_9_out, mem_error, halt);
  and and_1 (and_1_out, ~or_9_out, Clk_out);  // AND_Gate
  Counter #(.max('h9), .width(16)) counter_1 (
    .clr(or_8_out), .up(1'b1), .count(1'b1), .clk(and_1_out), .carry(counter_1_carry),
    .Q({counter_1_q_4, counter_1_q_3, counter_1_q_2, counter_1_q}));  // open: load, D
  Adder #(.width(16)) adder_1 (
    .a(PC[15:0]), .b({counter_1_q_4, counter_1_q_3, counter_1_q_2, counter_1_q}), .out(PC_Addr));  // open: cin, cout
  and and_2 (and_2_out, decoder_2_out2, or_5_out);
  Adder #(.width(16)) adder_2 (.a(PC[15:0]), .b(multiplexer_1_out), .out(adder_2_out));  // open: cin, cout
  Decoder #(.enable("false"), .select(4)) decoder_2 (
    .out0(decoder_2_out0), .out2(decoder_2_out2), .sel(counter_1_q));  // open: out1, out3, out4, out5, out6, out7, out8, out9, out10, out11, out12, out13, out14, out15
  Decoder #(.enable("false"), .select(4)) decoder_3 (
    .out1(decoder_3_out1), .out2(decoder_3_out2), .out3(decoder_3_out3), .out4(decoder_3_out4),
    .out5(decoder_3_out5), .out6(decoder_3_out6), .out7(decoder_3_out7), .out8(decoder_3_out8),
    .sel(demultiplexer_1_out1));  // open: out0, out9, out10, out11, out12, out13, out14, out15
  or or_10 (or_10_out, counter_1_carry, or_8_out);
  Decoder #(.enable("false"), .select(4)) decoder_4 (
    .out0(decoder_4_out0), .out1(decoder_4_out1), .out2(decoder_4_out2), .out3(decoder_4_out3),
    .out4(decoder_4_out4), .out5(decoder_4_out5), .out6(decoder_4_out6), .out7(decoder_4_out7),
    .out8(decoder_4_out8), .out9(decoder_4_out9), .sel(demultiplexer_1_out0));  // open: out10, out11, out12, out13, out14, out15
  Demultiplexer #(.width(4)) demultiplexer_1 (
    .out0(demultiplexer_1_out0), .out1(demultiplexer_1_out1), .in(counter_1_q), .sel(or_6_out));
  and and_3 (and_3_out, decoder_2_out0, decoder_4_out0);
  or or_11 (or_11_out, decoder_3_out1, decoder_4_out2);
  or or_12 (or_12_out, decoder_3_out2, decoder_4_out3);
  or or_13 (or_13_out, decoder_3_out3, decoder_4_out4);
  or or_14 (or_14_out, decoder_3_out4, decoder_4_out5);
  or or_15 (or_15_out, decoder_3_out5, decoder_4_out6);
  or or_16 (or_16_out, decoder_3_out6, decoder_4_out7);
  or or_17 (or_17_out, decoder_3_out7, decoder_4_out8);
  or or_18 (or_18_out, decoder_3_out8, decoder_4_out9);
  Register register_1 (.D(Inst_Comp), .en(or_11_out), .clk(and_1_out), .Q(register_1_q), .clr(Reset));
  Register register_2 (.D(Inst_Comp), .en(or_14_out), .clk(and_1_out), .Q(register_2_q), .clr(Reset));
  Register register_3 (.D(Inst_Comp), .en(or_12_out), .clk(and_1_out), .Q(register_3_q), .clr(Reset));
  Register register_4 (.D(Inst_Comp), .en(or_15_out), .clk(and_1_out), .Q(register_4_q), .clr(Reset));
  Register register_5 (.D(Inst_Comp), .en(or_18_out), .clk(and_1_out), .Q(register_5_q), .clr(Reset));
  Register register_6 (.D(Inst_Comp), .en(or_13_out), .clk(and_1_out), .Q(register_6_q), .clr(Reset));
  Register register_7 (.D(Inst_Comp), .en(or_16_out), .clk(and_1_out), .Q(register_7_q), .clr(Reset));
  Register register_8 (.D(Inst_Comp), .en(or_17_out), .clk(and_1_out), .Q(register_8_q), .clr(Reset));
  Register #(.width(4)) r_icode (.D(Inst_Comp[7:4]), .en(and_3_out), .clk(and_1_out), .Q(icode), .clr(Reset));
  Register #(.width(4)) r_ifun (.D(Inst_Comp[3:0]), .en(and_3_out), .clk(and_1_out), .Q(ifun), .clr(Reset));
  Register #(.width(4)) r_rA (.D(Inst_Comp[7:4]), .en(decoder_4_out1), .clk(and_1_out), .Q(rA), .clr(Reset));
  Register #(.width(4)) r_rB (.D(Inst_Comp[3:0]), .en(decoder_4_out1), .clk(and_1_out), .Q(rB), .clr(Reset));
  Register #(.width(64)) r_valC (
    .D({register_5_q, register_8_q, register_7_q, register_4_q, register_2_q, register_6_q, register_3_q, register_1_q}),
    .clk(and_1_out), .Q(valC), .clr(Reset));  // open: en
  Register #(.width(16)) r_valP (.D(adder_2_out), .clk(and_1_out), .Q(valP[15:0]), .clr(Reset));  // open: en
  Register #(.width(1)) register_9 (.D(decoder_1_out0), .clk(and_1_out), .Q(register_9_q), .clr(Reset));  // open: en
  and and_4 (and_4_out, decoder_1_out0, register_9_q);
  Register #(.width(1)) register_10 (.D(and_4_out), .clk(and_1_out), .Q(halt), .clr(Reset));  // open: en

  assign valP[63:16] = in_4;
endmodule

module Decode_Unit (
  input  [3:0] iCode,
  input  [3:0] rA,
  input  [3:0] rB,
  input  write_enable,
  input  [63:0] valE,
  input  reset,
  input  [63:0] valM,
  input  cond,
  output [63:0] valA,
  output [63:0] valB,
  output [63:0] reg14,
  output [63:0] reg9,
  output [63:0] regsi,
  output [63:0] reg13,
  output [63:0] reg8,
  output [63:0] regdx,
  output [63:0] reg12,
  output [63:0] regsp,
  output [63:0] regcx,
  output [63:0] reg11,
  output [63:0] regbp,
  output [63:0] regbx,
  output [63:0] reg10,
  output [63:0] regdi,
  output [63:0] regax
);

  wire and_1_out, and_2_out, clock_1_out, counter_1_q, decoder_1_out2, decoder_1_out3, decoder_1_out5,
       decoder_1_out6, decoder_1_out8, decoder_1_out9, decoder_1_out10, decoder_1_out11, decoder_2_out2,
       decoder_2_out8, decoder_2_out9, decoder_2_out10, decoder_2_out11, decoder_3_out0, decoder_3_out1,
       decoder_3_out2, decoder_3_out3, decoder_3_out4, decoder_3_out5, decoder_3_out6, decoder_3_out7,
       decoder_3_out8, decoder_3_out9, decoder_3_out10, decoder_3_out11, decoder_3_out12, decoder_3_out13,
       decoder_3_out14, multiplexer_1_out, multiplexer_3_out, not_1_out, not_2_out, or_1_out, or_2_out,
       or_3_out, or_4_out, or_5_out, or_6_out, or_7_out, or_8_out, or_9_out, or_10_out;
  wire [3:0] multiplexer_4_out, multiplexer_5_out, multiplexer_7_out, multiplexer_8_out;
  wire [63:0] multiplexer_2_out, multiplexer_6_out, register_1_q, register_2_q;

  and and_1 (and_1_out, ~decoder_2_out2, write_enable);  // AND_Gate
  and and_2 (and_2_out, write_enable, cond, decoder_2_out2);
  or or_1 (or_1_out, and_1_out, and_2_out);
  Decoder #(.select(4)) decoder_1 (
    .out2(decoder_1_out2), .out3(decoder_1_out3), .out5(decoder_1_out5), .out6(decoder_1_out6),
    .out8(decoder_1_out8), .out9(decoder_1_out9), .out10(decoder_1_out10), .out11(decoder_1_out11),
    .sel(iCode), .en(or_1_out));  // open: out0, out1, out4, out7, out12, out13, out14, out15
  or or_2 (or_2_out, decoder_1_out11, or_3_out);
  Register #(.width(64)) register_1 (.D(valE), .en(or_2_out), .clk(clock_1_out), .Q(register_1_q));  // open: clr
  Register #(.width(64)) register_2 (.D(valM), .en(or_4_out), .clk(clock_1_out), .Q(register_2_q));  // open: clr
  Decoder #(.enable("false"), .select(4)) decoder_2 (
    .out2(decoder_2_out2), .out8(decoder_2_out8), .out9(decoder_2_out9), .out10(decoder_2_out10),
    .out11(decoder_2_out11), .sel(iCode));  // open: out0, out1, out3, out4, out5, out6, out7, out12, out13, out14, out15
  or or_3 (or_3_out, decoder_1_out2, decoder_1_out3, decoder_1_out6, decoder_1_out8, decoder_1_out9, decoder_1_out10);
  or or_4 (or_4_out, decoder_1_out5, decoder_1_out11);
  not not_1 (not_1_out, or_3_out);
  Multiplexer multiplexer_1 (.in0(not_1_out), .in1(not_2_out), .out(multiplexer_1_out), .sel(decoder_1_out11));
  or or_5 (or_5_out, decoder_2_out8, decoder_2_out9, decoder_2_out11);
  Counter #(.max('h1), .width(1)) counter_1 (
    .clr(reset), .up(1'b1), .count(decoder_1_out11), .clk(clock_1_out), .Q(counter_1_q));  // open: load, D, carry
  not not_2 (not_2_out, counter_1_q);
  Multiplexer #(.width(64)) multiplexer_2 (
    .in0(register_1_q), .in1(register_2_q), .out(multiplexer_2_out), .sel(multiplexer_1_out));
  or or_6 (or_6_out, decoder_1_out5, decoder_1_out11);
  or or_7 (or_7_out, decoder_1_out8, decoder_1_out9, decoder_1_out10);
  Multiplexer multiplexer_3 (.in0(or_7_out), .in1(counter_1_q), .out(multiplexer_3_out), .sel(decoder_1_out11));
  or or_8 (or_8_out, decoder_1_out11, decoder_1_out5, or_3_out);
  Multiplexer #(.width(4)) multiplexer_4 (.in0(rB), .in1(rA), .out(multiplexer_4_out), .sel(or_6_out));
  Multiplexer #(.width(4)) multiplexer_5 (
    .in0(multiplexer_4_out), .in1(4'b0111), .out(multiplexer_5_out), .sel(multiplexer_3_out));
  Clock clock_1 (.out(clock_1_out));
  Decoder #(.select(4)) decoder_3 (
    .out0(decoder_3_out0), .out1(decoder_3_out1), .out2(decoder_3_out2), .out3(decoder_3_out3),
    .out4(decoder_3_out4), .out5(decoder_3_out5), .out6(decoder_3_out6), .out7(decoder_3_out7),
    .out8(decoder_3_out8), .out9(decoder_3_out9), .out10(decoder_3_out10), .out11(decoder_3_out11),
    .out12(decoder_3_out12), .out13(decoder_3_out13), .out14(decoder_3_out14), .sel(multiplexer_5_out),
    .en(or_8_out));  // open: out15
  Multiplexer #(.width(64)) multiplexer_6 (
    .in0(multiplexer_2_out), .in1(64'hffff), .out(multiplexer_6_out), .sel(reset));
  or or_9 (or_9_out, decoder_2_out10, or_5_out);
  Multiplexer #(.width(4)) multiplexer_7 (.in0(rA), .in1(4'b0111), .out(multiplexer_7_out), .sel(or_5_out));
  Multiplexer #(.width(4)) multiplexer_8 (.in0(rB), .in1(4'b0111), .out(multiplexer_8_out), .sel(or_9_out));
  Register #(.width(64)) rax (.D(multiplexer_6_out), .en(decoder_3_out0), .clk(clock_1_out), .Q(regax), .clr(reset));
  Register #(.width(64)) rbx (.D(multiplexer_6_out), .en(decoder_3_out1), .clk(clock_1_out), .Q(regbx), .clr(reset));
  Register #(.width(64)) rcx (.D(multiplexer_6_out), .en(decoder_3_out2), .clk(clock_1_out), .Q(regcx), .clr(reset));
  Register #(.width(64)) rdx (.D(multiplexer_6_out), .en(decoder_3_out3), .clk(clock_1_out), .Q(regdx), .clr(reset));
  Register #(.width(64)) rsi (.D(multiplexer_6_out), .en(decoder_3_out4), .clk(clock_1_out), .Q(regsi), .clr(reset));
  Register #(.width(64)) rdi (.D(multiplexer_6_out), .en(decoder_3_out5), .clk(clock_1_out), .Q(regdi), .clr(reset));
  Register #(.width(64)) rbp (.D(multiplexer_6_out), .en(decoder_3_out6), .clk(clock_1_out), .Q(regbp), .clr(reset));
  Register #(.width(64)) rsp (.D(multiplexer_6_out), .en(or_10_out), .clk(clock_1_out), .Q(regsp));  // open: clr
  or or_10 (or_10_out, decoder_3_out7, reset);
  Register #(.width(64)) r8 (.D(multiplexer_6_out), .en(decoder_3_out8), .clk(clock_1_out), .Q(reg8), .clr(reset));
  Register #(.width(64)) r9 (.D(multiplexer_6_out), .en(decoder_3_out9), .clk(clock_1_out), .Q(reg9), .clr(reset));
  Register #(.width(64)) r10 (.D(multiplexer_6_out), .en(decoder_3_out10), .clk(clock_1_out), .Q(reg10), .clr(reset));
  Register #(.width(64)) r11 (.D(multiplexer_6_out), .en(decoder_3_out11), .clk(clock_1_out), .Q(reg11), .clr(reset));
  Register #(.width(64)) r12 (.D(multiplexer_6_out), .en(decoder_3_out12), .clk(clock_1_out), .Q(reg12), .clr(reset));
  Register #(.width(64)) r13 (.D(multiplexer_6_out), .en(decoder_3_out13), .clk(clock_1_out), .Q(reg13), .clr(reset));
  Register #(.width(64)) r14 (.D(multiplexer_6_out), .en(decoder_3_out14), .clk(clock_1_out), .Q(reg14), .clr(reset));
  Multiplexer #(.select(4), .width(64)) multiplexer_9 (
    .in0(regax), .in1(regbx), .in2(regcx), .in3(regdx), .in4(regsi), .in5(regdi), .in6(regbp), .in7(regsp),
    .in8(reg8), .in9(reg9), .in10(reg10), .in11(reg11), .in12(reg12), .in13(reg13), .in14(reg14),
    .in15({64{1'b0}}), .out(valA), .sel(multiplexer_7_out));
  Multiplexer #(.select(4), .width(64)) multiplexer_10 (
    .in0(regax), .in1(regbx), .in2(regcx), .in3(regdx), .in4(regsi), .in5(regdi), .in6(regbp), .in7(regsp),
    .in8(reg8), .in9(reg9), .in10(reg10), .in11(reg11), .in12(reg12), .in13(reg13), .in14(reg14),
    .in15({64{1'b0}}), .out(valB), .sel(multiplexer_8_out));
endmodule

module Execute_Unit (
  input  [3:0] iCode,
  input  [3:0] iFun,
  input  [63:0] valA,
  input  [63:0] valC,
  input  [63:0] valB,
  output COND,
  output ZF,
  output SF,
  output OverF,
  output [63:0] valE
);

  wire and_1_out, and_3_out, and_4_out, and_5_out, and_6_out, and_7_out, and_8_out, and_9_out,
       comparator_1_eq, decoder_1_out1, decoder_1_out2, decoder_1_out3, decoder_1_out4, decoder_1_out5,
       decoder_1_out6, decoder_1_out8, decoder_1_out9, decoder_1_out10, decoder_1_out11, not_1_out,
       not_2_out, not_3_out, not_4_out, not_5_out, not_6_out, not_7_out, not_8_out, or_1_out, or_2_out,
       or_3_out, or_4_out, or_5_out, or_6_out, subtractor_1_bout, xnor_1_out, xor_2_out;
  wire [1:0] priority_encoder_2_out;
  wire [2:0] priority_encoder_1_out;
  wire [3:0] adder_3_out, multiplexer_3_out;
  wire [62:0] adder_2_out;
  wire [63:0] adder_1_out, and_2_out, multiplexer_1_out, multiplexer_2_out, subtractor_1_out, xor_1_out;
  wire [63:63] adder_2_out_2;

  Decoder #(.select(4)) decoder_1 (
    .out1(decoder_1_out1), .out2(decoder_1_out2), .out3(decoder_1_out3), .out4(decoder_1_out4),
    .out5(decoder_1_out5), .out6(decoder_1_out6), .out8(decoder_1_out8), .out9(decoder_1_out9),
    .out10(decoder_1_out10), .out11(decoder_1_out11), .sel(iCode));  // open: out0, out7, out12, out13, out14, out15, en
  or or_1 (or_1_out, decoder_1_out4, decoder_1_out3, decoder_1_out5);
  or or_2 (or_2_out, decoder_1_out2, decoder_1_out6);
  or or_3 (or_3_out, decoder_1_out9, decoder_1_out11);
  or or_4 (or_4_out, decoder_1_out8, decoder_1_out10);
  or or_5 (or_5_out, decoder_1_out2, decoder_1_out3);
  not not_1 (not_1_out, iCode[0]);
  and and_1 (and_1_out, not_1_out, iCode[1], iCode[2], not_2_out);
  not not_2 (not_2_out, iCode[3]);
  Priority_Encoder priority_encoder_1 (
    .in0(decoder_1_out1), .in1(or_1_out), .in2(or_2_out), .in3(or_3_out), .in4(or_4_out),
    .out(priority_encoder_1_out));  // open: in5, in6, in7, en_in, gs, en_out
  Multiplexer #(.select(3), .width(64)) multiplexer_1 (
    .in0({64{1'b0}}), .in1(valC), .in2(valA), .in3(64'h8), .in4(64'hfffffffffffffff8), .in5({64{1'b0}}),
    .out(multiplexer_1_out), .sel(priority_encoder_1_out));  // open: in6, in7
  Multiplexer #(.width(64)) multiplexer_2 (.in0(valB), .in1({64{1'b0}}), .out(multiplexer_2_out), .sel(or_5_out));
  Adder #(.width(64)) adder_1 (.a(multiplexer_1_out), .b(multiplexer_2_out), .out(adder_1_out));  // open: cin, cout
  Subtractor #(.width(64)) subtractor_1 (
    .a(multiplexer_2_out), .b(multiplexer_1_out), .out(subtractor_1_out), .bout(subtractor_1_bout));  // open: bin
  assign and_2_out = multiplexer_1_out & multiplexer_2_out;  // AND_Gate and_2, 64 bits wide
  assign xor_1_out = multiplexer_1_out ^ multiplexer_2_out;  // XOR_Gate xor_1, 64 bits wide
  and and_3 (and_3_out, not_3_out, iCode[2], iCode[1], not_4_out);
  not not_3 (not_3_out, iCode[3]);
  Adder #(.width(64)) adder_2 (
    .a(multiplexer_1_out), .b(multiplexer_2_out), .out({adder_2_out_2[63], adder_2_out}));  // open: cin, cout
  Multiplexer #(.width(4)) multiplexer_3 (.in0(4'b0000), .in1(iFun), .out(multiplexer_3_out), .sel(and_3_out));
  Adder #(.width(4)) adder_3 (.a(multiplexer_3_out), .b(4'b0001), .out(adder_3_out));  // open: cin, cout
  not not_4 (not_4_out, iCode[0]);
  Comparator #(.width(64)) comparator_1 (
    .a({64{1'b0}}), .b({adder_2_out_2[63], adder_2_out}), .eq(comparator_1_eq));  // open: gt, lt
  xor xor_2 (xor_2_out, adder_2_out_2[63], multiplexer_1_out[63]);
  Priority_Encoder #(.select(2)) priority_encoder_2 (
    .in0(adder_3_out[0]), .in1(adder_3_out[1]), .in2(adder_3_out[2]), .in3(adder_3_out[3]),
    .out(priority_encoder_2_out));  // open: gs, en_out, en_in
  xnor xnor_1 (xnor_1_out, multiplexer_2_out[63], multiplexer_1_out[63]);
  and and_4 (and_4_out, xnor_1_out, xor_2_out);
  Multiplexer #(.select(2), .width(64)) multiplexer_4 (
    .in0(adder_1_out), .in1(subtractor_1_out), .in2(and_2_out), .in3(xor_1_out), .out(valE),
    .sel(priority_encoder_2_out));
  D_Flip_Flop d_ff_1 (.D(comparator_1_eq), .clk(and_1_out), .Q(ZF));  // open: Qn, preset, reset
  D_Flip_Flop d_ff_2 (.D(adder_2_out_2[63]), .clk(and_1_out), .Q(SF));  // open: Qn, preset, reset
  D_Flip_Flop d_ff_3 (.D(and_4_out), .clk(and_1_out), .Q(OverF));  // open: Qn, preset, reset
  and and_5 (and_5_out, OverF, SF);
  and and_6 (and_6_out, OverF, SF);
  and and_7 (and_7_out, OverF, SF);
  and and_8 (and_8_out, SF, OverF);
  not not_5 (not_5_out, and_8_out);
  not not_6 (not_6_out, and_7_out);
  not not_7 (not_7_out, ZF);
  or or_6 (or_6_out, and_5_out, ZF);
  and and_9 (and_9_out, not_6_out, not_7_out);
  not not_8 (not_8_out, ZF);
  Multiplexer #(.select(4)) multiplexer_5 (
    .in0(1'b1), .in1(or_6_out), .in2(and_6_out), .in3(ZF), .in4(not_8_out), .in5(not_5_out), .in6(and_9_out),
    .out(COND), .sel(iFun));  // open: in7, in8, in9, in10, in11, in12, in13, in14, in15

  // Notes on the sheet:
  //   ALU_A
  //   SetCC
  //   ALU_B
  //   A
  //   B
  //   SetCC
  //   Check if the last bit is 1 
  //   valE
  //   CC
  //   COND
  //   jne
  //   jge
  //   jle
  //   jl
  //   je
endmodule

module Memory_Unit (
  input  [3:0] iCode,
  input  [63:0] valE,
  input  [63:0] valA,
  input  [63:0] valP,
  output w_Enable,
  output r_Enable,
  output [15:0] Addr,
  output [63:0] Data
);

  wire decoder_1_out4, decoder_1_out5, decoder_1_out8, decoder_1_out9, decoder_1_out10, decoder_1_out11,
       or_1_out;
  wire [63:16] multiplexer_1_out;

  Decoder #(.enable("false"), .select(4)) decoder_1 (
    .out4(decoder_1_out4), .out5(decoder_1_out5), .out8(decoder_1_out8), .out9(decoder_1_out9),
    .out10(decoder_1_out10), .out11(decoder_1_out11), .sel(iCode));  // open: out0, out1, out2, out3, out6, out7, out12, out13, out14, out15
  or or_1 (or_1_out, decoder_1_out9, decoder_1_out11);
  Multiplexer #(.width(64)) multiplexer_1 (.in0(valE), .in1(valA), .out({multiplexer_1_out, Addr}), .sel(or_1_out));
  Multiplexer #(.width(64)) multiplexer_2 (.in0(valA), .in1(valP), .out(Data), .sel(decoder_1_out8));
  or or_2 (r_Enable, decoder_1_out5, decoder_1_out11, decoder_1_out9);
  or or_3 (w_Enable, decoder_1_out10, decoder_1_out8, decoder_1_out4);
endmodule

module PCUpdate_Unit (
  input  [3:0] iCode,
  input  [63:0] valP,
  input  [63:0] valC,
  input  [63:0] valM,
  input  CND,
  output [63:0] PC
);

  wire and_1_out, and_2_out, decoder_1_out1, decoder_1_out2, decoder_1_out3, decoder_1_out4, decoder_1_out5,
       decoder_1_out6, decoder_1_out7, decoder_1_out8, decoder_1_out10, decoder_1_out11, not_1_out;
  wire [2:0] or_1_out;

  Decoder #(.select(4)) decoder_1 (
    .out1(decoder_1_out1), .out2(decoder_1_out2), .out3(decoder_1_out3), .out4(decoder_1_out4),
    .out5(decoder_1_out5), .out6(decoder_1_out6), .out7(decoder_1_out7), .out8(decoder_1_out8),
    .out9(or_1_out[2]), .out10(decoder_1_out10), .out11(decoder_1_out11), .sel(iCode));  // open: out0, out12, out13, out14, out15, en
  not not_1 (not_1_out, CND);
  and and_1 (and_1_out, decoder_1_out7, CND);
  and and_2 (and_2_out, decoder_1_out7, not_1_out);
  or or_1 (or_1_out[0], decoder_1_out1, decoder_1_out2, decoder_1_out3, decoder_1_out4, and_2_out, decoder_1_out5, decoder_1_out6, decoder_1_out10, decoder_1_out11);
  or or_2 (or_1_out[1], decoder_1_out8, and_1_out);
  Multiplexer #(.select(3), .width(64)) multiplexer_1 (
    .in1(valP), .in2(valC), .in4(valM), .out(PC), .sel(or_1_out));  // open: in0, in3, in5, in6, in7

  // Notes on the sheet:
  //   valC
  //   valM
  //   valP
endmodule
